# Fritzing sketch 230117-fritzing (saved by Fritzing 0.9.10b)

parts:
  Mod1 = Amica NodeMCU DEVKIT 1.0
  S1 = SWITCH-MOMENTARY-2 [package=tactile-pth]

nets:
  N1: Mod1.pin_9, Mod1.pin_25, S1.1
  N2: Mod1.pin_15, S1.2
